# Fritzing sketch drv8825_arduino (saved by Fritzing 0.9.3b)
breadboards: 1

parts:
  Z_as = DRV 8825 Stepper Motor Carrier, High Current [part_number="DRV 8825"]
  M2 = Stepper Motor - Bipolar  # not connected
  M3 = Stepper Motor - Bipolar  # not connected
  M4 = Stepper Motor - Bipolar
  X_as = DRV 8825 Stepper Motor Carrier, High Current [part_number="DRV 8825"]
  Part1 = Arduino Ethernet Shield (Rev3)
  Y_as = DRV 8825 Stepper Motor Carrier, High Current [part_number="DRV 8825"]
  Power_12V = Power plug
  Power_5V = Power plug  # not connected

nets:
  N1: Z_as.VOLTAGE_ST/_MT, X_as.VOLTAGE_ST/_MT, Y_as.VOLTAGE_ST/_MT, Power_12V.VCC
  N2: Z_as.GROUND_ST/_MT, X_as.GROUND_ST/_MT, Y_as.GROUND_ST/_MT, Power_12V.GND
  N3: M4.A, X_as.OUT_2B
  N4: M4.C, X_as.OUT_2A
  N5: M4.B, X_as.OUT_1A
  N6: M4.D, X_as.OUT_1B
  N7: X_as.STEP, Part1.D2
  N8: X_as.DIRECTION, Part1.PWM_D5
